# Fritzing sketch nixie (saved by Fritzing 0.9.3b)
circuit board: 8.46667cm x 5.64444cm
breadboards: 2

parts:
  Part1 = TracoPower TSR-1 DC/DC Converter [part_number="TSR 1-2450"]
  J1 = Power Jack [package=power_jack_smd]
  U1 = atmega328 [package=dip]
  R1 = Resistor [tolerance=±5% resistance=10k package=THT]
  XTAL1 = Crystal [frequency="16 Mhz" package=SMD]
  C1 = Capacitor [package=cap-pth-small2]
  C2 = Capacitor [package=cap-pth-small2]
  Part2 = Real Time Clock Module - DS1307 RTC Breakout Board

nets:
  N1: Part1.1, J1.GND
  GND: Part1.2, J1.GNDBREAK, U1.GND, R1.Pin_1, C1.1, C2.2, Part2.GND
  VCC: Part1.3, U1.VCC, U1.AVCC, Part2.5V
  N2: U1.RESET, R1.Pin_0
  N3: U1.XLAT1, XTAL1.pin_1, C2.1
  N4: U1.XLAT2, XTAL1.pin_0, C1.2
  N5: U1.A4, Part2.SQW
  N6: U1.A5, Part2.SCL

custom parts:
  TracoPower TSR-1 DC/DC Converter: TracoPower TSR 1-2450 DC Converter Input6.5 - 36VDC Max current 1A
